// Logisim project CRC.circ as structural Verilog: 2 circuits, main circuit CRC
module CRC (
  input  [7:0] A,
  input  [3:0] B,
  output [10:0] C
);

  wire [3:1] div_2_c, div_3_c, div_4_c, div_5_c, div_6_c, div_7_c, div_8_c;

  div div_1 (.A({div_2_c, 1'b0}), .B(B), .C(C[2:0]));  // open: D
  div div_2 (.A({div_3_c, 1'b0}), .B(B), .C(div_2_c));  // open: D
  div div_3 (.A({div_4_c, 1'b0}), .B(B), .C(div_3_c));  // open: D
  div div_4 (.A({div_5_c, A[0]}), .B(B), .C(div_4_c));  // open: D
  div div_5 (.A({div_6_c, A[1]}), .B(B), .C(div_5_c));  // open: D
  div div_6 (.A({div_7_c, A[2]}), .B(B), .C(div_6_c));  // open: D
  div div_7 (.A({div_8_c, A[3]}), .B(B), .C(div_7_c));  // open: D
  div div_8 (.A(A[7:4]), .B(B), .C(div_8_c));  // open: D

  assign C[10:3] = A;
endmodule

module div (
  input  [3:0] A,
  input  [3:0] B,
  output [2:0] C,
  output D
);

  wire and_1_out, and_2_out, and_3_out, and_4_out;

  and and_1 (and_1_out, B[0], A[3]);
  and and_2 (and_2_out, B[1], A[3]);
  and and_3 (and_3_out, B[2], A[3]);
  and and_4 (and_4_out, B[3], A[3]);
  xor xor_1 (C[0], A[0], and_1_out);
  xor xor_2 (C[1], A[1], and_2_out);
  xor xor_3 (C[2], A[2], and_3_out);
  // XOR_Gate xor_4 has open pins: in0=A[3], in1=and_4_out, out=open

  assign D = A[3];
endmodule
