// Logisim project Fibonacci.circ as structural Verilog: 1 circuit, main circuit main
module main (
  input  [31:0] in_1,
  output [31:0] out_2
);

  wire and_1_out, and_3_out, \begin , clock_1_out, comparator_2_eq, count_2_q, d_ff_1_q, \end , not_1_out,
       not_2_out, not_3_out, not_4_out, not_5_out, not_6_out, not_7_out, not_8_out, or_1_out, or_2_out,
       or_3_out, or_4_out, or_5_out, test, xor_1_out;
  wire [1:0] count_q;
  wire [31:0] A00, A01, A10, A11, and_2_out, B00, B01, B10, B11, counter_1_q, multiplexer_1_out,
       multiplexer_2_out, multiplexer_3_out, multiplexer_4_out, multiplexer_5_out, multiplexer_6_out,
       multiplexer_7_out, multiplexer_8_out, multiplexer_9_out, multiplier_1_out, multiplier_2_out,
       multiplier_3_out, multiplier_4_out, multiplier_5_out, multiplier_6_out, multiplier_7_out,
       multiplier_8_out, register_3_q, shifter_1_out, X0, X1, X2, X3;

  not not_1 (not_1_out, test);
  Clock clock_1 (.out(clock_1_out));
  Counter #(.width(2), .max('h3)) count (.Q(count_q), .clk(not_3_out));  // open: load, D, count, carry, clr
  Counter #(.width(32), .max('hffffffff)) counter_1 (
    .count(not_1_out), .Q(counter_1_q), .clk(not_2_out));  // open: load, D, carry, clr
  not not_2 (not_2_out, not_3_out);
  not not_3 (not_3_out, clock_1_out);
  // Probe on counter_1_q
  // Probe on in_1
  or or_1 (or_1_out, \begin , and_1_out);
  not not_4 (not_4_out, not_3_out);
  Register #(.width(32)) register_1 (.D(X0), .en(or_1_out), .Q(A00), .clk(not_3_out));  // open: clr
  Register #(.width(32)) register_2 (.D(X2), .en(and_1_out), .Q(A10), .clk(not_3_out));  // open: clr
  Register #(.width(32)) register_3 (
    .D(multiplexer_1_out), .en(\end ), .Q(register_3_q), .clk(not_3_out));  // open: clr
  Multiplexer #(.width(32), .enable("false")) multiplexer_1 (
    .in0(in_1), .in1(shifter_1_out), .out(multiplexer_1_out), .sel(not_5_out));
  not not_5 (not_5_out, test);
  and and_1 (and_1_out, not_4_out, \end , not_8_out);
  or or_2 (or_2_out, and_1_out, \begin );
  Comparator #(.width(32)) comparator_1 (.a({32{1'b0}}), .b(register_3_q), .eq(test));  // open: gt, lt
  Register #(.width(32)) register_4 (.D(X1), .en(and_1_out), .Q(A01), .clk(not_3_out));  // open: clr
  Register #(.width(32)) register_5 (.D(X3), .en(or_2_out), .Q(A11), .clk(not_3_out));  // open: clr
  not not_6 (not_6_out, not_3_out);
  not not_7 (not_7_out, not_3_out);
  assign and_2_out = 32'h1 & register_3_q;  // AND_Gate and_2, 32 bits wide
  Shifter #(.width(32), .shift("lr")) shifter_1 (.in(register_3_q), .\dist (5'b00001), .out(shifter_1_out));
  Register #(.width(32)) register_6 (.D(X0), .en(or_3_out), .Q(B00), .clk(not_6_out));  // open: clr
  or or_3 (or_3_out, \begin , and_3_out);
  Register #(.width(32)) register_7 (.D(X2), .en(or_4_out), .Q(B10), .clk(not_7_out));  // open: clr
  or or_4 (or_4_out, \begin , and_3_out);
  Comparator #(.width(32)) comparator_2 (.a({32{1'b0}}), .b(and_2_out), .eq(comparator_2_eq));  // open: gt, lt
  xor xor_1 (xor_1_out, and_3_out, \begin );
  not not_8 (not_8_out, comparator_2_eq);
  and and_3 (and_3_out, not_3_out, \end );
  or or_5 (or_5_out, \begin , and_3_out);
  Register #(.width(32), .trigger("high")) register_8 (.D(A01), .en(test), .Q(out_2), .clk(not_3_out));  // open: clr
  Register #(.width(32)) register_9 (.D(X1), .en(or_5_out), .Q(B01), .clk(not_6_out));  // open: clr
  Register #(.width(32)) register_10 (.D(X3), .en(xor_1_out), .Q(B11), .clk(not_7_out));  // open: clr
  // Probe on out_2
  D_Flip_Flop d_ff_1 (.clk(not_3_out), .D(test), .Q(d_ff_1_q));  // open: Qn, preset, en, reset
  Multiplexer #(.width(32), .enable("false")) multiplexer_2 (
    .in0(A00), .in1(B00), .out(multiplexer_2_out), .sel(not_3_out));
  Multiplier #(.width(32)) multiplier_1 (.a(multiplexer_2_out), .b(B00), .out(multiplier_1_out));  // open: cin, cout
  Multiplexer #(.width(32), .enable("false")) multiplexer_3 (
    .in0(A01), .in1(B01), .out(multiplexer_3_out), .sel(not_3_out));
  Multiplier #(.width(32)) multiplier_2 (.a(multiplexer_3_out), .b(B10), .out(multiplier_2_out));  // open: cin, cout
  Multiplexer #(.width(32), .enable("false")) multiplexer_4 (
    .in0(A00), .in1(B00), .out(multiplexer_4_out), .sel(not_3_out));
  Multiplier #(.width(32)) multiplier_3 (.a(multiplexer_4_out), .b(B01), .out(multiplier_3_out));  // open: cin, cout
  Multiplexer #(.width(32), .enable("false")) multiplexer_5 (
    .in0(A01), .in1(B01), .out(multiplexer_5_out), .sel(not_3_out));
  Multiplier #(.width(32)) multiplier_4 (.a(multiplexer_5_out), .b(B11), .out(multiplier_4_out));  // open: cin, cout
  Multiplexer #(.width(32), .enable("false")) multiplexer_6 (
    .in0(A10), .in1(B10), .out(multiplexer_6_out), .sel(not_3_out));
  Multiplier #(.width(32)) multiplier_5 (.a(multiplexer_6_out), .b(B00), .out(multiplier_5_out));  // open: cin, cout
  Multiplexer #(.width(32), .enable("false")) multiplexer_7 (
    .in0(A11), .in1(B11), .out(multiplexer_7_out), .sel(not_3_out));
  Multiplier #(.width(32)) multiplier_6 (.a(multiplexer_7_out), .b(B10), .out(multiplier_6_out));  // open: cin, cout
  Multiplexer #(.width(32), .enable("false")) multiplexer_8 (
    .in0(A10), .in1(B10), .out(multiplexer_8_out), .sel(not_3_out));
  Multiplier #(.width(32)) multiplier_7 (.a(multiplexer_8_out), .b(B01), .out(multiplier_7_out));  // open: cin, cout
  Multiplexer #(.width(32), .enable("false")) multiplexer_9 (
    .in0(A11), .in1(B11), .out(multiplexer_9_out), .sel(not_3_out));
  Multiplier #(.width(32)) multiplier_8 (.a(multiplexer_9_out), .b(B11), .out(multiplier_8_out));  // open: cin, cout
  Counter #(.width(1), .max('h1)) count_2 (.Q(count_2_q), .clk(test));  // open: load, D, count, carry, clr
  not not_9 (\end , count_2_q);
  Adder #(.width(32)) adder_1 (.a(multiplier_1_out), .b(multiplier_2_out), .out(X0), .cin(\begin ));  // open: cout
  Adder #(.width(32)) adder_2 (.a(multiplier_3_out), .b(multiplier_4_out), .out(X1), .cin(\begin ));  // open: cout
  Adder #(.width(32)) adder_3 (.a(multiplier_5_out), .b(multiplier_6_out), .out(X2), .cin(\begin ));  // open: cout
  Adder #(.width(32)) adder_4 (.a(multiplier_7_out), .b(multiplier_8_out), .out(X3), .cin(\begin ));  // open: cout
  and and_4 (\begin , \end , d_ff_1_q);
endmodule
