// Logisim project fsm.circ as structural Verilog: 3 circuits, main circuit fsm
module fsm (
  input  CLR,
  input  [1:0] In,
  output Z
);

  wire clock_1_out;
  wire [1:0] and_1_out, register_1_q, t_state_1_next_state;
  wire [1:1] not_1_out;

  Clock clock_1 (.out(clock_1_out));
  not not_1 (not_1_out[1], CLR);
  T_State t_state_1 (.In(In), .State(register_1_q), .Next_State(t_state_1_next_state));
  assign and_1_out = t_state_1_next_state & {2{not_1_out[1]}};  // AND_Gate and_1, 2 bits wide
  Register #(.width(2)) register_1 (.D(and_1_out), .Q(register_1_q), .clk(clock_1_out));  // open: en, clr
  Output output_1 (.In(In), .State(register_1_q), .OutPut(Z));
endmodule

module Output (
  input  [1:0] In,
  input  [1:0] State,
  output OutPut
);

  wire not_1_out;

  not not_1 (not_1_out, In[0]);
  and and_1 (OutPut, not_1_out, State[1]);
endmodule

module T_State (
  input  [1:0] In,
  input  [1:0] State,
  output [1:0] Next_State
);

  wire and_2_out, and_3_out, not_1_out, not_2_out, not_3_out, not_4_out, not_5_out;

  not not_1 (not_1_out, In[0]);
  not not_2 (not_2_out, State[1]);
  not not_3 (not_3_out, In[1]);
  not not_4 (not_4_out, In[0]);
  not not_5 (not_5_out, State[1]);
  and and_1 (Next_State[1], not_1_out, not_2_out, State[0]);
  and and_2 (and_2_out, not_3_out, In[0]);
  and and_3 (and_3_out, In[1], not_4_out, not_5_out, State[0]);
  or or_1 (Next_State[0], and_2_out, and_3_out);
endmodule
