// Logisim project grf.circ as structural Verilog: 1 circuit, main circuit grf
module grf (
  input  clk,
  input  reset,
  input  WE,
  input  [4:0] A1,
  input  [4:0] A2,
  input  [4:0] A3,
  input  [31:0] WD,
  output [31:0] RD1,
  output [31:0] RD2
);

  wire demultiplexer_2_out0, demultiplexer_2_out1, demultiplexer_2_out2, demultiplexer_2_out3,
       demultiplexer_2_out4, demultiplexer_2_out5, demultiplexer_2_out6, demultiplexer_2_out7,
       demultiplexer_3_out0, demultiplexer_3_out1, demultiplexer_3_out2, demultiplexer_3_out3,
       demultiplexer_3_out4, demultiplexer_3_out5, demultiplexer_3_out6, demultiplexer_3_out7,
       demultiplexer_4_out0, demultiplexer_4_out1, demultiplexer_4_out2, demultiplexer_4_out3,
       demultiplexer_4_out4, demultiplexer_4_out5, demultiplexer_4_out6, demultiplexer_4_out7,
       demultiplexer_5_out0, demultiplexer_5_out1, demultiplexer_5_out2, demultiplexer_5_out3,
       demultiplexer_5_out4, demultiplexer_5_out5, demultiplexer_5_out6, demultiplexer_5_out7, sel_we0,
       sel_we1, sel_we2, sel_we3;
  wire [31:0] DATA0, DATA1, DATA2, DATA3, DATA4, DATA5, DATA6, DATA7, DATA8, DATA9, DATA10, DATA11, DATA12,
       DATA13, DATA14, DATA15, DATA16, DATA17, DATA18, DATA19, DATA20, DATA21, DATA22, DATA23, DATA24,
       DATA25, DATA26, DATA27, DATA28, DATA29, DATA30, DATA31;

  Demultiplexer #(.select(2), .enable("false")) demultiplexer_1 (
    .out0(sel_we0), .out1(sel_we1), .out2(sel_we2), .out3(sel_we3), .in(WE), .sel(A3[4:3]));
  Demultiplexer #(.select(3), .enable("false")) demultiplexer_2 (
    .out0(demultiplexer_2_out0), .out1(demultiplexer_2_out1), .out2(demultiplexer_2_out2),
    .out3(demultiplexer_2_out3), .out4(demultiplexer_2_out4), .out5(demultiplexer_2_out5),
    .out6(demultiplexer_2_out6), .out7(demultiplexer_2_out7), .in(sel_we0), .sel(A3[2:0]));
  Register #(.width(32)) register_1 (.D(WD), .en(1'b0), .Q(DATA0), .clk(clk), .clr(reset));
  Register #(.width(32)) register_2 (.D(WD), .en(demultiplexer_2_out1), .Q(DATA1), .clk(clk), .clr(reset));
  Register #(.width(32)) register_3 (.D(WD), .en(demultiplexer_2_out2), .Q(DATA2), .clk(clk), .clr(reset));
  Register #(.width(32)) register_4 (.D(WD), .en(demultiplexer_2_out3), .Q(DATA3), .clk(clk), .clr(reset));
  Register #(.width(32)) register_5 (.D(WD), .en(demultiplexer_2_out4), .Q(DATA4), .clk(clk), .clr(reset));
  Register #(.width(32)) register_6 (.D(WD), .en(demultiplexer_2_out5), .Q(DATA5), .clk(clk), .clr(reset));
  Register #(.width(32)) register_7 (.D(WD), .en(demultiplexer_2_out6), .Q(DATA6), .clk(clk), .clr(reset));
  Register #(.width(32)) register_8 (.D(WD), .en(demultiplexer_2_out7), .Q(DATA7), .clk(clk), .clr(reset));
  Demultiplexer #(.select(3), .enable("false")) demultiplexer_3 (
    .out0(demultiplexer_3_out0), .out1(demultiplexer_3_out1), .out2(demultiplexer_3_out2),
    .out3(demultiplexer_3_out3), .out4(demultiplexer_3_out4), .out5(demultiplexer_3_out5),
    .out6(demultiplexer_3_out6), .out7(demultiplexer_3_out7), .in(sel_we1), .sel(A3[2:0]));
  Register #(.width(32)) register_9 (.D(WD), .en(demultiplexer_3_out0), .Q(DATA8), .clk(clk), .clr(reset));
  Register #(.width(32)) register_10 (.D(WD), .en(demultiplexer_3_out1), .Q(DATA9), .clk(clk), .clr(reset));
  Register #(.width(32)) register_11 (.D(WD), .en(demultiplexer_3_out2), .Q(DATA10), .clk(clk), .clr(reset));
  Register #(.width(32)) register_12 (.D(WD), .en(demultiplexer_3_out3), .Q(DATA11), .clk(clk), .clr(reset));
  Register #(.width(32)) register_13 (.D(WD), .en(demultiplexer_3_out4), .Q(DATA12), .clk(clk), .clr(reset));
  Register #(.width(32)) register_14 (.D(WD), .en(demultiplexer_3_out5), .Q(DATA13), .clk(clk), .clr(reset));
  Register #(.width(32)) register_15 (.D(WD), .en(demultiplexer_3_out6), .Q(DATA14), .clk(clk), .clr(reset));
  Register #(.width(32)) register_16 (.D(WD), .en(demultiplexer_3_out7), .Q(DATA15), .clk(clk), .clr(reset));
  Demultiplexer #(.select(3), .enable("false")) demultiplexer_4 (
    .out0(demultiplexer_4_out0), .out1(demultiplexer_4_out1), .out2(demultiplexer_4_out2),
    .out3(demultiplexer_4_out3), .out4(demultiplexer_4_out4), .out5(demultiplexer_4_out5),
    .out6(demultiplexer_4_out6), .out7(demultiplexer_4_out7), .in(sel_we2), .sel(A3[2:0]));
  Register #(.width(32)) register_17 (.D(WD), .en(demultiplexer_4_out0), .Q(DATA16), .clk(clk), .clr(reset));
  Register #(.width(32)) register_18 (.D(WD), .en(demultiplexer_4_out1), .Q(DATA17), .clk(clk), .clr(reset));
  Register #(.width(32)) register_19 (.D(WD), .en(demultiplexer_4_out2), .Q(DATA18), .clk(clk), .clr(reset));
  Register #(.width(32)) register_20 (.D(WD), .en(demultiplexer_4_out3), .Q(DATA19), .clk(clk), .clr(reset));
  Register #(.width(32)) register_21 (.D(WD), .en(demultiplexer_4_out4), .Q(DATA20), .clk(clk), .clr(reset));
  Register #(.width(32)) register_22 (.D(WD), .en(demultiplexer_4_out5), .Q(DATA21), .clk(clk), .clr(reset));
  Register #(.width(32)) register_23 (.D(WD), .en(demultiplexer_4_out6), .Q(DATA22), .clk(clk), .clr(reset));
  Register #(.width(32)) register_24 (.D(WD), .en(demultiplexer_4_out7), .Q(DATA23), .clk(clk), .clr(reset));
  Demultiplexer #(.select(3), .enable("false")) demultiplexer_5 (
    .out0(demultiplexer_5_out0), .out1(demultiplexer_5_out1), .out2(demultiplexer_5_out2),
    .out3(demultiplexer_5_out3), .out4(demultiplexer_5_out4), .out5(demultiplexer_5_out5),
    .out6(demultiplexer_5_out6), .out7(demultiplexer_5_out7), .in(sel_we3), .sel(A3[2:0]));
  Register #(.width(32)) register_25 (.D(WD), .en(demultiplexer_5_out0), .Q(DATA24), .clk(clk), .clr(reset));
  Register #(.width(32)) register_26 (.D(WD), .en(demultiplexer_5_out1), .Q(DATA25), .clk(clk), .clr(reset));
  Register #(.width(32)) register_27 (.D(WD), .en(demultiplexer_5_out2), .Q(DATA26), .clk(clk), .clr(reset));
  Register #(.width(32)) register_28 (.D(WD), .en(demultiplexer_5_out3), .Q(DATA27), .clk(clk), .clr(reset));
  Register #(.width(32)) register_29 (.D(WD), .en(demultiplexer_5_out4), .Q(DATA28), .clk(clk), .clr(reset));
  Register #(.width(32)) register_30 (.D(WD), .en(demultiplexer_5_out5), .Q(DATA29), .clk(clk), .clr(reset));
  Register #(.width(32)) register_31 (.D(WD), .en(demultiplexer_5_out6), .Q(DATA30), .clk(clk), .clr(reset));
  Register #(.width(32)) register_32 (.D(WD), .en(demultiplexer_5_out7), .Q(DATA31), .clk(clk), .clr(reset));
  Multiplexer #(.select(5), .width(32), .enable("false")) multiplexer_1 (
    .in0(DATA0), .in1(DATA1), .in2(DATA2), .in3(DATA3), .in4(DATA4), .in5(DATA5), .in6(DATA6), .in7(DATA7),
    .in8(DATA8), .in9(DATA9), .in10(DATA10), .in11(DATA11), .in12(DATA12), .in13(DATA13), .in14(DATA14),
    .in15(DATA15), .in16(DATA16), .in17(DATA17), .in18(DATA18), .in19(DATA19), .in20(DATA20), .in21(DATA21),
    .in22(DATA22), .in23(DATA23), .in24(DATA24), .in25(DATA25), .in26(DATA26), .in27(DATA27), .in28(DATA28),
    .in29(DATA29), .in30(DATA30), .in31(DATA31), .out(RD1), .sel(A1));
  Multiplexer #(.select(5), .width(32), .enable("false")) multiplexer_2 (
    .in0(DATA0), .in1(DATA1), .in2(DATA2), .in3(DATA3), .in4(DATA4), .in5(DATA5), .in6(DATA6), .in7(DATA7),
    .in8(DATA8), .in9(DATA9), .in10(DATA10), .in11(DATA11), .in12(DATA12), .in13(DATA13), .in14(DATA14),
    .in15(DATA15), .in16(DATA16), .in17(DATA17), .in18(DATA18), .in19(DATA19), .in20(DATA20), .in21(DATA21),
    .in22(DATA22), .in23(DATA23), .in24(DATA24), .in25(DATA25), .in26(DATA26), .in27(DATA27), .in28(DATA28),
    .in29(DATA29), .in30(DATA30), .in31(DATA31), .out(RD2), .sel(A2));

  // Other names for the same wires on the sheet: LOWER_3bit[2:0] = A3[2:0]; RST = reset
endmodule
