// Logisim project mod5.circ as structural Verilog: 1 circuit, main circuit mod5
module mod5 (
  input  In,
  output s0,
  output s1,
  output s2,
  output s3,
  output s4
);

  wire clock_1_out;
  wire [1:1] d_ff_1_q;

  Clock clock_1 (.out(clock_1_out));
  D_Flip_Flop d_ff_1 (.clk(clock_1_out), .D(In), .Q(d_ff_1_q[1]));  // open: Qn, preset, en, reset
  D_Flip_Flop d_ff_2 (.clk(clock_1_out), .D(d_ff_1_q[1]));  // open: Q, Qn, preset, en, reset
  Decoder #(.select(2)) decoder_1 (.out0(s1), .out1(s2), .out2(s4), .out3(s3), .sel({d_ff_1_q[1], In}));  // open: en

  assign s0 = 1'b0;
endmodule
