// Logisim project CPU.circ as structural Verilog: 8 circuits, main circuit main
module main (
  input  Reset,
  output [31:0] Instr,
  output RegWrite,
  output [4:0] RegAddr,
  output [31:0] RegData,
  output MemWrite,
  output [4:0] MemAddr,
  output [31:0] MemData
);

  wire BSel, CLK, NPCOp, WDSel, WRSel, zero;
  wire [1:0] ALUOp, EXTOp;
  wire [31:0] alu_1_c, dm_1_rd, ext_1_ext32, grf_1_rd1, multiplexer_3_out;

  Clock clock_1 (.out(CLK));
  IFU ifu_1 (.CLK(CLK), .RST(Reset), .NPCOp(NPCOp), .INSTR(Instr), .IMM(Instr[15:0]));
  Control control_1 (
    .opcode(Instr[31:26]), .funct(Instr[5:0]), .DMWr(MemWrite), .ALUOp(ALUOp), .BSel(BSel), .EXTOp(EXTOp),
    .RFWr(RegWrite), .WDSel(WDSel), .WRSel(WRSel), .NPCOp(NPCOp), .Zero(zero));
  Multiplexer #(.width(5), .enable("false")) multiplexer_1 (
    .in0(Instr[20:16]), .in1(Instr[15:11]), .out(RegAddr), .sel(WRSel));
  Multiplexer #(.width(32), .enable("false")) multiplexer_2 (.in0(alu_1_c), .in1(dm_1_rd), .out(RegData), .sel(WDSel));
  EXT ext_1 (.IMM(Instr[15:0]), .EXTOp(EXTOp), .EXT32(ext_1_ext32));
  grf grf_1 (
    .A1(Instr[25:21]), .A2(Instr[20:16]), .A3(RegAddr), .WD(RegData), .RD1(grf_1_rd1), .RD2(MemData),
    .CLK(CLK), .RST(Reset), .WE(RegWrite));
  Multiplexer #(.width(32), .enable("false")) multiplexer_3 (
    .in0(MemData), .in1(ext_1_ext32), .out(multiplexer_3_out), .sel(BSel));
  ALU alu_1 (.A(grf_1_rd1), .B(multiplexer_3_out), .ALUOp(ALUOp), .C(alu_1_c), .Zero(zero));
  DM dm_1 (.Addr(alu_1_c), .WD(MemData), .WE(MemWrite), .CLK(CLK), .RD(dm_1_rd), .RST(Reset), .testAdr(MemAddr));

  // Other names for the same wires on the sheet: DMWr = MemWrite; RFWr = RegWrite
endmodule

module grf (
  input  CLK,
  input  RST,
  input  WE,
  input  [4:0] A1,
  input  [4:0] A2,
  input  [4:0] A3,
  input  [31:0] WD,
  output [31:0] RD1,
  output [31:0] RD2
);

  wire demultiplexer_2_out0, demultiplexer_2_out1, demultiplexer_2_out2, demultiplexer_2_out3,
       demultiplexer_2_out4, demultiplexer_2_out5, demultiplexer_2_out6, demultiplexer_2_out7,
       demultiplexer_3_out0, demultiplexer_3_out1, demultiplexer_3_out2, demultiplexer_3_out3,
       demultiplexer_3_out4, demultiplexer_3_out5, demultiplexer_3_out6, demultiplexer_3_out7,
       demultiplexer_4_out0, demultiplexer_4_out1, demultiplexer_4_out2, demultiplexer_4_out3,
       demultiplexer_4_out4, demultiplexer_4_out5, demultiplexer_4_out6, demultiplexer_4_out7,
       demultiplexer_5_out0, demultiplexer_5_out1, demultiplexer_5_out2, demultiplexer_5_out3,
       demultiplexer_5_out4, demultiplexer_5_out5, demultiplexer_5_out6, demultiplexer_5_out7, sel_we0,
       sel_we1, sel_we2, sel_we3;
  wire [31:0] DATA0, DATA1, DATA2, DATA3, DATA4, DATA5, DATA6, DATA7, DATA8, DATA9, DATA10, DATA11, DATA12,
       DATA13, DATA14, DATA15, DATA16, DATA17, DATA18, DATA19, DATA20, DATA21, DATA22, DATA23, DATA24,
       DATA25, DATA26, DATA27, DATA28, DATA29, DATA30, DATA31;

  Demultiplexer #(.select(2), .enable("false")) demultiplexer_1 (
    .out0(sel_we0), .out1(sel_we1), .out2(sel_we2), .out3(sel_we3), .in(WE), .sel(A3[4:3]));
  Demultiplexer #(.select(3), .enable("false")) demultiplexer_2 (
    .out0(demultiplexer_2_out0), .out1(demultiplexer_2_out1), .out2(demultiplexer_2_out2),
    .out3(demultiplexer_2_out3), .out4(demultiplexer_2_out4), .out5(demultiplexer_2_out5),
    .out6(demultiplexer_2_out6), .out7(demultiplexer_2_out7), .in(sel_we0), .sel(A3[2:0]));
  Register #(.width(32)) register_1 (.D(WD), .en(1'b0), .Q(DATA0), .clk(CLK), .clr(RST));
  Register #(.width(32)) register_2 (.D(WD), .en(demultiplexer_2_out1), .Q(DATA1), .clk(CLK), .clr(RST));
  Register #(.width(32)) register_3 (.D(WD), .en(demultiplexer_2_out2), .Q(DATA2), .clk(CLK), .clr(RST));
  Register #(.width(32)) register_4 (.D(WD), .en(demultiplexer_2_out3), .Q(DATA3), .clk(CLK), .clr(RST));
  Register #(.width(32)) register_5 (.D(WD), .en(demultiplexer_2_out4), .Q(DATA4), .clk(CLK), .clr(RST));
  Register #(.width(32)) register_6 (.D(WD), .en(demultiplexer_2_out5), .Q(DATA5), .clk(CLK), .clr(RST));
  Register #(.width(32)) register_7 (.D(WD), .en(demultiplexer_2_out6), .Q(DATA6), .clk(CLK), .clr(RST));
  Register #(.width(32)) register_8 (.D(WD), .en(demultiplexer_2_out7), .Q(DATA7), .clk(CLK), .clr(RST));
  Demultiplexer #(.select(3), .enable("false")) demultiplexer_3 (
    .out0(demultiplexer_3_out0), .out1(demultiplexer_3_out1), .out2(demultiplexer_3_out2),
    .out3(demultiplexer_3_out3), .out4(demultiplexer_3_out4), .out5(demultiplexer_3_out5),
    .out6(demultiplexer_3_out6), .out7(demultiplexer_3_out7), .in(sel_we1), .sel(A3[2:0]));
  Register #(.width(32)) register_9 (.D(WD), .en(demultiplexer_3_out0), .Q(DATA8), .clk(CLK), .clr(RST));
  Register #(.width(32)) register_10 (.D(WD), .en(demultiplexer_3_out1), .Q(DATA9), .clk(CLK), .clr(RST));
  Register #(.width(32)) register_11 (.D(WD), .en(demultiplexer_3_out2), .Q(DATA10), .clk(CLK), .clr(RST));
  Register #(.width(32)) register_12 (.D(WD), .en(demultiplexer_3_out3), .Q(DATA11), .clk(CLK), .clr(RST));
  Register #(.width(32)) register_13 (.D(WD), .en(demultiplexer_3_out4), .Q(DATA12), .clk(CLK), .clr(RST));
  Register #(.width(32)) register_14 (.D(WD), .en(demultiplexer_3_out5), .Q(DATA13), .clk(CLK), .clr(RST));
  Register #(.width(32)) register_15 (.D(WD), .en(demultiplexer_3_out6), .Q(DATA14), .clk(CLK), .clr(RST));
  Register #(.width(32)) register_16 (.D(WD), .en(demultiplexer_3_out7), .Q(DATA15), .clk(CLK), .clr(RST));
  Demultiplexer #(.select(3), .enable("false")) demultiplexer_4 (
    .out0(demultiplexer_4_out0), .out1(demultiplexer_4_out1), .out2(demultiplexer_4_out2),
    .out3(demultiplexer_4_out3), .out4(demultiplexer_4_out4), .out5(demultiplexer_4_out5),
    .out6(demultiplexer_4_out6), .out7(demultiplexer_4_out7), .in(sel_we2), .sel(A3[2:0]));
  Register #(.width(32)) register_17 (.D(WD), .en(demultiplexer_4_out0), .Q(DATA16), .clk(CLK), .clr(RST));
  Register #(.width(32)) register_18 (.D(WD), .en(demultiplexer_4_out1), .Q(DATA17), .clk(CLK), .clr(RST));
  Register #(.width(32)) register_19 (.D(WD), .en(demultiplexer_4_out2), .Q(DATA18), .clk(CLK), .clr(RST));
  Register #(.width(32)) register_20 (.D(WD), .en(demultiplexer_4_out3), .Q(DATA19), .clk(CLK), .clr(RST));
  Register #(.width(32)) register_21 (.D(WD), .en(demultiplexer_4_out4), .Q(DATA20), .clk(CLK), .clr(RST));
  Register #(.width(32)) register_22 (.D(WD), .en(demultiplexer_4_out5), .Q(DATA21), .clk(CLK), .clr(RST));
  Register #(.width(32)) register_23 (.D(WD), .en(demultiplexer_4_out6), .Q(DATA22), .clk(CLK), .clr(RST));
  Register #(.width(32)) register_24 (.D(WD), .en(demultiplexer_4_out7), .Q(DATA23), .clk(CLK), .clr(RST));
  Demultiplexer #(.select(3), .enable("false")) demultiplexer_5 (
    .out0(demultiplexer_5_out0), .out1(demultiplexer_5_out1), .out2(demultiplexer_5_out2),
    .out3(demultiplexer_5_out3), .out4(demultiplexer_5_out4), .out5(demultiplexer_5_out5),
    .out6(demultiplexer_5_out6), .out7(demultiplexer_5_out7), .in(sel_we3), .sel(A3[2:0]));
  Register #(.width(32)) register_25 (.D(WD), .en(demultiplexer_5_out0), .Q(DATA24), .clk(CLK), .clr(RST));
  Register #(.width(32)) register_26 (.D(WD), .en(demultiplexer_5_out1), .Q(DATA25), .clk(CLK), .clr(RST));
  Register #(.width(32)) register_27 (.D(WD), .en(demultiplexer_5_out2), .Q(DATA26), .clk(CLK), .clr(RST));
  Register #(.width(32)) register_28 (.D(WD), .en(demultiplexer_5_out3), .Q(DATA27), .clk(CLK), .clr(RST));
  Register #(.width(32)) register_29 (.D(WD), .en(demultiplexer_5_out4), .Q(DATA28), .clk(CLK), .clr(RST));
  Register #(.width(32)) register_30 (.D(WD), .en(demultiplexer_5_out5), .Q(DATA29), .clk(CLK), .clr(RST));
  Register #(.width(32)) register_31 (.D(WD), .en(demultiplexer_5_out6), .Q(DATA30), .clk(CLK), .clr(RST));
  Register #(.width(32)) register_32 (.D(WD), .en(demultiplexer_5_out7), .Q(DATA31), .clk(CLK), .clr(RST));
  Multiplexer #(.select(5), .width(32), .enable("false")) multiplexer_1 (
    .in0(DATA0), .in1(DATA1), .in2(DATA2), .in3(DATA3), .in4(DATA4), .in5(DATA5), .in6(DATA6), .in7(DATA7),
    .in8(DATA8), .in9(DATA9), .in10(DATA10), .in11(DATA11), .in12(DATA12), .in13(DATA13), .in14(DATA14),
    .in15(DATA15), .in16(DATA16), .in17(DATA17), .in18(DATA18), .in19(DATA19), .in20(DATA20), .in21(DATA21),
    .in22(DATA22), .in23(DATA23), .in24(DATA24), .in25(DATA25), .in26(DATA26), .in27(DATA27), .in28(DATA28),
    .in29(DATA29), .in30(DATA30), .in31(DATA31), .out(RD1), .sel(A1));
  Multiplexer #(.select(5), .width(32), .enable("false")) multiplexer_2 (
    .in0(DATA0), .in1(DATA1), .in2(DATA2), .in3(DATA3), .in4(DATA4), .in5(DATA5), .in6(DATA6), .in7(DATA7),
    .in8(DATA8), .in9(DATA9), .in10(DATA10), .in11(DATA11), .in12(DATA12), .in13(DATA13), .in14(DATA14),
    .in15(DATA15), .in16(DATA16), .in17(DATA17), .in18(DATA18), .in19(DATA19), .in20(DATA20), .in21(DATA21),
    .in22(DATA22), .in23(DATA23), .in24(DATA24), .in25(DATA25), .in26(DATA26), .in27(DATA27), .in28(DATA28),
    .in29(DATA29), .in30(DATA30), .in31(DATA31), .out(RD2), .sel(A2));

  // Other names for the same wires on the sheet: LOWER_3bit[2:0] = A3[2:0]
endmodule

module DM (
  input  [31:0] Addr,
  input  [31:0] WD,
  input  WE,
  input  CLK,
  input  RST,
  output [4:0] testAdr,
  output [31:0] RD
);

  wire [1:0] bit_extender_1_out;

  Bit_Extender #(.in_width(32), .out_width(7)) bit_extender_1 (.in(Addr), .out({testAdr, bit_extender_1_out}));
  RAM #(.addrWidth(5), .dataWidth(32), .bus("separate")) ram_1 (
    .addr(testAdr), .din(WD), .data(RD), .str(WE), .clk(CLK), .clr(RST));  // open: sel, ld
endmodule

module EXT (
  input  [15:0] IMM,
  input  [1:0] EXTOp,
  output [31:0] EXT32
);

  wire [31:0] bit_extender_1_out, bit_extender_2_out;

  assign bit_extender_1_out = {{16{1'b0}}, IMM};  // Bit_Extender bit_extender_1
  assign bit_extender_2_out = {{16{IMM[15]}}, IMM};  // Bit_Extender bit_extender_2
  Multiplexer #(.select(2), .width(32), .enable("false")) multiplexer_1 (
    .in0(bit_extender_1_out), .in1(bit_extender_2_out), .in2({IMM, {16{1'b0}}}), .out(EXT32), .sel(EXTOp));  // open: in3
endmodule

module ALU (
  input  [31:0] A,
  input  [31:0] B,
  input  [1:0] ALUOp,
  output [31:0] C,
  output Zero
);

  wire and_1_out, and_2_out;
  wire [31:0] adder_1_out, multiplexer_1_out, not_1_out, or_1_out;

  Multiplexer #(.width(32), .enable("false")) multiplexer_1 (
    .in0(B), .in1(not_1_out), .out(multiplexer_1_out), .sel(and_1_out));
  assign not_1_out = ~B;  // NOT_Gate not_1, 32 bits wide
  and and_1 (and_1_out, ALUOp[0], ~ALUOp[1]);  // AND_Gate
  Adder #(.width(32)) adder_1 (.a(A), .b(multiplexer_1_out), .out(adder_1_out), .cin(and_1_out));  // open: cout
  assign or_1_out = A | multiplexer_1_out;  // OR_Gate or_1, 32 bits wide
  Multiplexer #(.width(32), .enable("false")) multiplexer_2 (
    .in0(adder_1_out), .in1(or_1_out), .out(C), .sel(and_2_out));
  and and_2 (and_2_out, ~ALUOp[0], ALUOp[1]);  // AND_Gate
  Comparator #(.width(32), .mode("unsigned")) comparator_1 (
    .a(adder_1_out), .b({32{1'b0}}), .eq(Zero));  // open: gt, lt
endmodule

module Control (
  input  [5:0] opcode,
  input  [5:0] funct,
  input  Zero,
  output DMWr,
  output [1:0] ALUOp,
  output BSel,
  output [1:0] EXTOp,
  output RFWr,
  output WDSel,
  output WRSel,
  output NPCOp
);

  wire ADDU, BEQ, not_1_out, not_2_out, not_3_out, not_4_out, not_5_out, not_6_out, not_7_out, not_8_out,
       not_9_out, not_10_out, not_11_out, not_12_out, not_13_out, not_14_out, not_15_out, not_16_out,
       not_17_out, not_18_out, not_19_out, not_20_out, not_21_out, not_22_out, not_23_out, not_24_out,
       not_25_out, not_26_out, not_27_out, not_28_out, not_29_out, not_30_out, not_31_out, not_32_out,
       not_33_out, not_34_out, SUBU;

  not not_1 (not_1_out, opcode[0]);
  not not_2 (not_2_out, opcode[1]);
  not not_3 (not_3_out, opcode[2]);
  not not_4 (not_4_out, opcode[3]);
  not not_5 (not_5_out, opcode[4]);
  not not_6 (not_6_out, opcode[5]);
  not not_7 (not_7_out, funct[2]);
  not not_8 (not_8_out, funct[3]);
  not not_9 (not_9_out, funct[4]);
  not not_10 (not_10_out, opcode[2]);
  and and_1 (WDSel, opcode[0], opcode[1], not_10_out, not_11_out, not_12_out, opcode[5]);
  not not_11 (not_11_out, opcode[3]);
  not not_12 (not_12_out, opcode[4]);
  not not_13 (not_13_out, opcode[0]);
  not not_14 (not_14_out, opcode[1]);
  and and_2 (BEQ, not_13_out, not_14_out, opcode[2], not_15_out, not_16_out, not_17_out);
  not not_15 (not_15_out, opcode[3]);
  not not_16 (not_16_out, opcode[4]);
  not not_17 (not_17_out, opcode[5]);
  and and_3 (SUBU, not_1_out, not_2_out, not_3_out, not_4_out, not_5_out, not_6_out, funct[0], funct[1], not_7_out, not_8_out, not_9_out, funct[5]);
  not not_18 (not_18_out, opcode[2]);
  not not_19 (not_19_out, opcode[4]);
  not not_20 (not_20_out, opcode[1]);
  not not_21 (not_21_out, opcode[4]);
  not not_22 (not_22_out, opcode[5]);
  not not_23 (not_23_out, opcode[0]);
  not not_24 (not_24_out, opcode[1]);
  not not_25 (not_25_out, opcode[2]);
  not not_26 (not_26_out, opcode[3]);
  not not_27 (not_27_out, opcode[4]);
  not not_28 (not_28_out, opcode[5]);
  not not_29 (not_29_out, funct[1]);
  not not_30 (not_30_out, funct[2]);
  not not_31 (not_31_out, funct[3]);
  not not_32 (not_32_out, funct[4]);
  and and_4 (DMWr, opcode[0], opcode[1], not_18_out, opcode[3], not_19_out, opcode[5]);
  and and_5 (ALUOp[1], opcode[0], not_20_out, opcode[2], opcode[3], not_21_out, not_22_out);
  and and_6 (ADDU, not_23_out, not_24_out, not_25_out, not_26_out, not_27_out, not_28_out, funct[0], not_29_out, not_30_out, not_31_out, not_32_out, funct[5]);
  and and_7 (EXTOp[1], opcode[0], opcode[1], opcode[2], opcode[3], not_33_out, not_34_out);
  not not_33 (not_33_out, opcode[4]);
  not not_34 (not_34_out, opcode[5]);
  or or_1 (ALUOp[0], SUBU, BEQ);
  or or_2 (BSel, ALUOp[1], DMWr, WDSel, EXTOp[1]);
  or or_3 (EXTOp[0], DMWr, WDSel);
  or or_4 (RFWr, WDSel, ALUOp[1], EXTOp[1], SUBU, ADDU);
  or or_5 (WRSel, SUBU, ADDU);
  and and_8 (NPCOp, BEQ, Zero);

  // Other names for the same wires on the sheet: ORI = ALUOp[1]; LUI = EXTOp[1]; funct_0 = funct[0];
  //   funct_1 = funct[1]; funct_2 = funct[2]; funct_3 = funct[3]; funct_4 = funct[4]; funct_5 = funct[5]; LW = WDSel;
  //   op_0 = opcode[0]; op_1 = opcode[1]; op_2 = opcode[2]; op_3 = opcode[3]; op_4 = opcode[4]; op_5 = opcode[5];
  //   SW = DMWr
endmodule

module IFU (
  input  CLK,
  input  RST,
  input  NPCOp,
  input  [15:0] IMM,
  output [31:0] INSTR
);

  wire [4:0] bit_extender_1_out;
  wire [31:0] adder_1_out, adder_2_out, bit_extender_2_out, NPC, PC_q, shifter_1_out;

  Register #(.width(32)) PC (.D(NPC), .Q(PC_q), .clk(CLK), .clr(RST));  // open: en
  Shifter #(.width(32), .shift("lr")) shifter_1 (.in(PC_q), .\dist (5'b00010), .out(shifter_1_out));
  Bit_Extender #(.in_width(32), .out_width(5)) bit_extender_1 (.in(shifter_1_out), .out(bit_extender_1_out));
  Adder #(.width(32)) adder_1 (.a(PC_q), .b(32'h4), .out(adder_1_out));  // open: cin, cout
  assign bit_extender_2_out = {{14{IMM[15]}}, {IMM, 2'b00}};  // Bit_Extender bit_extender_2
  ROM #(.addrWidth(5), .dataWidth(32)) rom_1 (.addr(bit_extender_1_out), .data(INSTR));  // open: sel
  Adder #(.width(32)) adder_2 (.a(adder_1_out), .b(bit_extender_2_out), .out(adder_2_out));  // open: cin, cout
  Multiplexer #(.width(32), .enable("false")) multiplexer_1 (
    .in0(adder_1_out), .in1(adder_2_out), .out(NPC), .sel(NPCOp));

  // Notes on the sheet:
  //   contents of rom_1 (hex, n*v repeats v):
  //   34080001 82021
endmodule

module NPC (
  input  [31:0] PC,
  input  [25:0] IMM,
  input  [31:0] RA,
  input  [1:0] NPCOp,
  output [31:0] NPC,
  output [31:0] PC4
);

  wire [31:0] adder_2_out, bit_extender_1_out;

  Adder #(.width(32)) adder_1 (.a(PC), .b(32'h4), .out(PC4));  // open: cin, cout
  assign bit_extender_1_out = {{14{IMM[15]}}, {IMM[15:0], 2'b00}};  // Bit_Extender bit_extender_1
  Adder #(.width(32)) adder_2 (.a(PC4), .b(bit_extender_1_out), .out(adder_2_out));  // open: cin, cout
  Multiplexer #(.select(2), .width(32), .enable("false")) multiplexer_1 (
    .in0(PC4), .in1(adder_2_out), .in2({PC[31:28], IMM, 2'b00}), .in3(RA), .out(NPC), .sel(NPCOp));
endmodule
